# Fritzing sketch layout (saved by Fritzing 1.0.7)
breadboards: 1

parts:
  U1 = ESP32S-HiLetgo [part_number=ESP32S-HiLetgo]
  M1 = RioRand LM2596
  A1 = Motor driver tzt DRV8833
  Q3 = MOSFET-NCHANNEL [package=to220v]
  VCC1 = 4 x AAA Battery Mount [internal_resistance=0.1Ω]  # not connected
  M2 = gear-motor
  M3 = DC Motor [voltage_(max)=6V voltage_(min)=3V]
  M4 = gear-motor
  J1 = Basic Servo
  JP4 = Header 2 [package=jst-2-pth]
  J2 = female pin header, 2 pins [form="♀ (female)"]

nets:
  GND: U1.GND, M1.Pin_4, A1.Pin_10, Q3.S, J1.gnd
  VIN: U1.VIN, M1.Pin_3, J1.vcc
  N1: U1.GPIO17, J1.pulse
  N2: U1.GPIO18, A1.Pin_12
  N3: U1.GPIO19, A1.Pin_11
  N4: U1.GPIO21, A1.Pin_8
  N5: U1.GPIO22, A1.Pin_7
  N6: U1.GPIO23, Q3.G
  N7: M1.Pin_1, M3.pin_1, JP4.2, J2.pin1
  N8: M1.Pin_2, JP4.1
  N9: A1.Pin_2, M4.pin_2
  N10: A1.Pin_3, M4.pin_1
  N11: A1.Pin_4, M2.pin_2
  N12: A1.Pin_5, M2.pin_1
  N13: Q3.D, M3.pin_2, J2.pin2

custom parts:
  ESP32S-HiLetgo: HiLetgo ESP-WROOM-32 ESP32 ESP-32S Development Board 2.4GHz Dual-Mode WiFi + Bluetooth Dual Cores Microcontroller The ESP32 integrated with Antenna switches, RF Balun, power amplifiers, low-noise amplifiers, filters, and management modules, and the entire solution occupies the least area of PCB. 2.4 GHz Wi-Fi plus Bluetooth dual-mode chip, with TSMC Ultra-low power consumption 40nm technology,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
  Motor driver tzt DRV8833: TZT DRV8833 DC3V-10V 1.5A 2 Channel DC Motor Drive Module.
